# Fritzing sketch c0bra-hp (saved by Fritzing 0.8.5b)
breadboards: 1

parts:
  Part1 = Barometric Pressure Sensor - BMP085 Breakout  # not connected
  R1 = Resistor [tolerance=±5% resistance=220 package=THT]
  R2 = Resistor [tolerance=±5% resistance=220 package=THT]
  Part2 = Barometric Pressure Sensor - BMP085 Breakout
  R3 = Resistor [tolerance=±5% resistance=220 package=THT]
  R4 = Resistor [tolerance=±5% resistance=220 package=THT]
  Part3 = Arduino Uno (Rev3) - ICSP
  RHT1 = Humidity and Temperature Sensor RHT03
  RHT2 = Humidity and Temperature Sensor RHT03
  R5 = Resistor [tolerance=±5% resistance=220 package=THT]
  R6 = Resistor [tolerance=±5% resistance=220 package=THT]

nets:
  VCC: R1.Pin_0, R2.Pin_0, Part2.SDA, R3.Pin_0, RHT1.Vcc, RHT2.Vcc, R5.Pin_0, R6.Pin_0
  N1: R1.Pin_1, Part2.EOC, R3.Pin_1, Part3.A5/SCL
  N2: R2.Pin_1, Part2.VCC, R4.Pin_1, Part3.A4/SDA
  N3: Part2.XCLR, RHT1.GND_2, RHT2.GND_2
  N4: Part2.SCL, R4.Pin_0
  N5: Part3.D4, RHT2.Data-signal, R6.Pin_1
  N6: Part3.D5_PWM, RHT1.Data-signal, R5.Pin_1
